# Fritzing sketch Uno-esp8266 (saved by Fritzing 0.9.5d)
breadboards: 1

parts:
  Part1 = Arduino Uno (Rev3) - ICSP
  U1 = LCD-16X2 [package=lcd-16x2_noholes]  # not connected
  R1 = Trimmer Potentiometer [maximum_resistance=10kΩ package=THT]
  DHT1 = DHT11 Humitidy and Temperature Sensor
  Espessif_Serial_Wifi_Modul_1 = ESP8266 ESP01 [part_number=ESP8266 package=THT]
  Part2 = GUVA-S12SD UV Light Sensor

nets:
  N1: Part1.A0, Part2.Out
  GND: Part1.GND, R1.leg2, DHT1.GND, Espessif_Serial_Wifi_Modul_1.GND
  N2: Part1.D2, Espessif_Serial_Wifi_Modul_1.TXD
  N3: Part1.D3_PWM, Espessif_Serial_Wifi_Modul_1.RXD
  N4: Part1.D4, DHT1.DATA
  3V3: Part1.3V3, Espessif_Serial_Wifi_Modul_1.VCC
  N5: Part1.5V, R1.leg1

custom parts:
  DHT11 Humitidy and Temperature Sensor: DHT11 Humidity and Temperature Sensor
  ESP8266 ESP01: Generic WiFi Module based on the ESP8266 with onboard PCB antenna and UART communications
  GUVA-S12SD UV Light Sensor: Extend your light-sensing spectrum with this analog UV sensor module. It uses a UV photodiode, which can detect the 240-370nm range of light (which covers UVB and most of UVA spectrum). The signal level from the photodiode is very small, in the nano-ampere level, so we tossed on an opamp to amplify the signal to a more manageable volt-level.
